# Fritzing sketch fiware-iot-upo (saved by Fritzing 0.9.3b)
breadboards: 1

parts:
  Componente1 = Arduino MKR1000
  T1 = LM35 Temperature Sensor [package="TO92 [THT]"]
  J1 = Piezo Speaker

nets:
  N1: Componente1.A0_DAC0, T1.Vout
  GND: Componente1.GND, T1.GND, J1.pin1
  N2: Componente1.VCC, T1.+Vs, J1.pin2

custom parts:
  Arduino MKR1000: MKR1000 is a powerful board that combines the functionality of the Zero and the Wi-Fi Shield. It is the ideal solution for makers wanting to design IoT projects with minimal previous experience in networking
